# Fritzing sketch ad9850 (saved by Fritzing 0.9.2b)
breadboards: 1

parts:
  Part1 = Arduino Uno (Rev3)
  AD1 = DDS AD9850

nets:
  N1: Part1.D8, AD1.CLK
  N2: Part1.D9_PWM, AD1.FQ
  N3: Part1.D10_PWM/SS, AD1.DATA
  N4: Part1.D11_PWM/MOSI, AD1.RST
  5V: Part1.5V, AD1.VCC
  GND: Part1.GND, AD1.GND

custom parts:
  DDS AD9850: AD9850 DDS Signal Generator Module, frequency range 0 to 40MHz, sine or square wave output, on board 70MHz low pass filter, and 125MHz clock module. https://code.google.com/p/ad9850-arduino/
