# Fritzing sketch signal_gen_2amps (saved by Fritzing 0.9.3b)
perfboards: 1

parts:
  AD1 = DDS AD9850
  R1 = Resistor [tolerance=±5% resistance=68k package=THT]
  C1 = Electrolytic Capacitor [capacitance=10µF voltage=35V package="100 mil [THT, electrolytic]"]
  U2 = POT [package=pot_alpha_rv16af-20]
  C2 = Electrolytic Capacitor [capacitance=0.22mF voltage=16V package="100 mil [THT, electrolytic]"]
  U1 = LM386 [package=dip08]
  C3 = Electrolytic Capacitor [capacitance=0.1mF voltage=16V package="100 mil [THT, electrolytic]"]
  C4 = Tantalum Capacitor [capacitance=10nF voltage=16V package="100 mil [THT, tantalum]"]
  J1 = female pin header, 2 pins [form="♀ (female)"]
  J2 = female pin header, 6 pins [form="♀ (female)"]
  U3 = LM386 [package=dip08]
  R2 = Resistor [tolerance=±5% resistance=68k package=THT]
  C5 = Electrolytic Capacitor [capacitance=10µF voltage=35V package="100 mil [THT, electrolytic]"]
  U4 = POT [package=pot_alpha_rv16af-20]
  C6 = Electrolytic Capacitor [capacitance=0.22mF voltage=16V package="100 mil [THT, electrolytic]"]
  C8 = Tantalum Capacitor [capacitance=10nF voltage=16V package="100 mil [THT, tantalum]"]
  J3 = female pin header, 3 pins [form="♀ (female)"]

nets:
  12V: AD1.VCC, U1.V+, C3.+, J1.pin2, J2.pin6, U3.V+
  GND: AD1.GND, R1.Pin_0, U2.E, U1.-IN, U1.V-, C3.-, C4.-, J1.pin1, J2.pin1, U3.-IN, R2.Pin_0, U4.E, J3.pin2
  N1: AD1.CLK, J2.pin5
  N2: AD1.FQ, J2.pin4
  N3: AD1.DATA, J2.pin3
  N4: AD1.RST, J2.pin2
  N5: AD1.SINA, C5.+
  N6: AD1.SINB, C1.+
  N7: R1.Pin_1, C1.-, U2.A
  N8: U2.S, U1.+IN, C4.+
  N9: C2.-, J3.pin1
  N10: C2.+, U1.OUT
  N11: U3.+IN, U4.S, C8.+
  N12: U3.V-, C8.-
  N13: U3.OUT, C6.+
  N14: R2.Pin_1, C5.-, U4.A
  N15: C6.-, J3.pin3

notes:
  RST / DATA / FQUD / CLK

custom parts:
  DDS AD9850: AD9850 DDS Signal Generator Module, frequency range 0 to 40MHz, sine or square wave output, on board 70MHz low pass filter, and 125MHz clock module. https://code.google.com/p/ad9850-arduino/
