# Fritzing sketch signal_gen_3board (saved by Fritzing 0.9.3b)
perfboards: 1

parts:
  AD1 = DDS AD9850
  J1 = female pin header, 3 pins [form="♀ (female)"]
  J2 = female pin header, 4 pins [form="♀ (female)"]
  R1 = Resistor [tolerance=±5% resistance=68k package=THT]
  C1 = Electrolytic Capacitor [capacitance=10µF voltage=35V package="100 mil [THT, electrolytic]"]
  U2 = POT [package=pot_alpha_rv16af-20]
  C2 = Electrolytic Capacitor [capacitance=0.22mF voltage=16V package="100 mil [THT, electrolytic]"]
  J3 = female pin header, 2 pins [form="♀ (female)"]
  U1 = LM386 [package=dip08]
  C3 = Electrolytic Capacitor [capacitance=0.1mF voltage=16V package="100 mil [THT, electrolytic]"]
  C4 = Tantalum Capacitor [capacitance=10nF voltage=16V package="100 mil [THT, tantalum]"]

nets:
  12V: AD1.VCC, J1.pin2, J1.pin3, U1.V+, C3.+
  GND: AD1.GND, J1.pin1, R1.Pin_0, U2.E, J3.pin2, U1.-IN, U1.V-, C3.-
  N1: AD1.CLK, J2.pin4
  N2: AD1.FQ, J2.pin3
  N3: AD1.DATA, J2.pin2
  N4: AD1.RST, J2.pin1
  N5: AD1.SINB, C1.+
  N6: C1.-, U2.A
  N7: U2.S, U1.+IN, C4.+
  N8: C2.-, J3.pin1
  N9: C2.+, U1.OUT

notes:
  RST / DATA / FQUD / CLK

custom parts:
  DDS AD9850: AD9850 DDS Signal Generator Module, frequency range 0 to 40MHz, sine or square wave output, on board 70MHz low pass filter, and 125MHz clock module. https://code.google.com/p/ad9850-arduino/
